# Fritzing sketch CanSat (saved by Fritzing 0.9.3b)
breadboards: 2

parts:
  Temp_+_Pressure = Adafruit_BMP280
  Controller = Arduino Uno (Rev3)
  Gyro = InvenSense MPU6050
  Outside_Temp = LM35 Temperature Sensor [package="TO92 [THT]"]
  XBee = XBee Explorer Regulated
  VCC1 = Battery block 9V

nets:
  3.3V: Temp_+_Pressure.3.3V, Controller.3V3
  GND: Temp_+_Pressure.GND, Controller.GND, Gyro.GND, Gyro.AD0, Outside_Temp.GND, XBee.GND, VCC1.-
  N1: Temp_+_Pressure.SCK/SCL, Controller.D13/SCK
  N2: Temp_+_Pressure.SDO/ADR, Controller.D12/MISO
  N3: Temp_+_Pressure.SDI/SDA, Controller.D11_PWM/MOSI
  N4: Temp_+_Pressure.CS, Controller.D10_PWM/SS
  N5: Controller.A0, Outside_Temp.Vout
  N6: Controller.A4/SDA, Gyro.SDA
  N7: Controller.A5/SCL, Gyro.SCL
  N8: Controller.D0/RX, XBee.DOUT
  N9: Controller.D1/TX, XBee.DIN
  5V: Controller.5V, Gyro.VCC, Outside_Temp.+Vs, XBee.5V
  N10: Controller.VIN, VCC1.+

custom parts:
  Adafruit_BMP280: Bosch has stepped up their game with their new BMP280 sensor, an environmental sensor with temperature, barometric pressure that is the next generation upgrade to the BMP085/BMP180/BMP183. This sensor is great for all sorts of weather sensing and can even be used in both I2C and SPI! This precision sensor from Bosch is the best low-cost, precision sensing solution for measuring barometric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
